# Fritzing sketch MIDI_DIN-Socket_Input (saved by Fritzing 0.9.2b)
breadboards: 1

parts:
  Arduino = Arduino Uno (Rev3)
  optocoupler = IC, DIP package, 8 pins [chip_label=6N138]
  R1 = Resistor [tolerance=±5% resistance=220 package=THT]
  R2 = Resistor [tolerance=±5% resistance=220 package=THT]
  R3 = Resistor [tolerance=±5% resistance=4.7k package=THT]
  1N4148 = Diode [package=diode-1n4148]
  MIDI_Socket = DIN-5 jack (MIDI) [package=THT]

nets:
  N1: Arduino.GND, optocoupler.pin5, R3.Pin_1
  N2: Arduino.D0/RX, optocoupler.pin6, R2.Pin_1
  N3: Arduino.5V, optocoupler.pin8, R2.Pin_0
  N4: optocoupler.pin2, R1.Pin_1, 1N4148.C
  N5: optocoupler.pin3, 1N4148.A, MIDI_Socket.5
  N6: optocoupler.pin7, R3.Pin_0
  N7: R1.Pin_0, MIDI_Socket.4
